# Fritzing sketch framework (saved by Fritzing 0.9.3b)
circuit board: 8.46667cm x 5.64444cm
breadboards: 1

parts:
  Arduino_Uno_R3 = Arduino Uno (Rev3)
  128*64LCD = 128 x 64 Graphic LCD
  电位器 = POT [package=pot_mammoth]
  SIM800C通讯模块 = SIM800L [package=THT]
  红外非接触体温 = MLX90614 [package=to-39]
  超声波传感器 = hc-sr04
  DHT11温湿度传感器 = Humidity and Temperature Sensor RHT03
  心率传感器（代替） = LilyPad Tri-Color LED
  J1 = Basic Servo
  U1 = GAS_SENSOR [package=mq-3]
  火焰传感器 = TSOP312.., 314.. [package=THT]

nets:
  N1: Arduino_Uno_R3.A0, 心率传感器（代替）.R
  N2: Arduino_Uno_R3.A1, U1.B1, U1.A1
  N3: Arduino_Uno_R3.A3, 火焰传感器.Data
  N4: Arduino_Uno_R3.A4/SDA, 红外非接触体温.PWM_SDA
  N5: Arduino_Uno_R3.A5/SCL, 红外非接触体温.SCL_VZ
  N6: Arduino_Uno_R3.D8, 128*64LCD.4_D/I
  N7: Arduino_Uno_R3.D9_PWM, 128*64LCD.5_R/W
  GND: Arduino_Uno_R3.GND, 128*64LCD.1_Vss, 128*64LCD.15_CS1, SIM800C通讯模块.GND, 红外非接触体温.VSS, 超声波传感器.GND, DHT11温湿度传感器.GND_2, 心率传感器（代替）.G, J1.gnd, U1.H1, 火焰传感器.GND
  N8: Arduino_Uno_R3.D0/RX, SIM800C通讯模块.SIM_TXD
  N9: Arduino_Uno_R3.D1/TX, SIM800C通讯模块.SIM_RXD
  N10: Arduino_Uno_R3.D3_PWM, 128*64LCD.6_Enable
  N11: Arduino_Uno_R3.D4, DHT11温湿度传感器.Data-signal
  N12: Arduino_Uno_R3.D5_PWM, J1.pulse
  N13: Arduino_Uno_R3.D6_PWM, 超声波传感器.Echo
  N14: Arduino_Uno_R3.D7, 超声波传感器.Trig
  5V: Arduino_Uno_R3.5V, 128*64LCD.2_Vdd, 电位器.S, SIM800C通讯模块.5V, 红外非接触体温.VDD, 超声波传感器.VCC, 心率传感器（代替）.B, J1.vcc, U1.H2, 火焰传感器.Vs
  N15: 128*64LCD.3_Vo, 电位器.A
  N16: 128*64LCD.18_Vout, 电位器.E

notes:
  青少年科技创新大赛
  开封高中 1812 李晨阳
